# Fritzing sketch composite (saved by Fritzing 0.9.3b)
breadboards: 1

parts:
  Pico1 = Raspberry Pi Pico
  R2 = Resistor [tolerance=±5% resistance=320 package=THT]
  R3 = Resistor [tolerance=±5% resistance=320 package=THT]
  R4 = Resistor [tolerance=±5% resistance=320 package=THT]
  R5 = Resistor [tolerance=±5% resistance=320 package=THT]
  R7 = Resistor [tolerance=±5% resistance=180 package=THT]
  R8 = Resistor [tolerance=±5% resistance=180 package=THT]
  R9 = Resistor [tolerance=±5% resistance=180 package=THT]
  R10 = Resistor [tolerance=±5% resistance=180 package=THT]
  R11 = Resistor [tolerance=±5% resistance=180 package=THT]
  R12 = Resistor [tolerance=±5% resistance=180 package=THT]
  R14 = Resistor [tolerance=±5% resistance=320 package=THT]
  R15 = Resistor [tolerance=±5% resistance=320 package=THT]
  R17 = Resistor [tolerance=±5% resistance=320 package=THT]
  R18 = Resistor [tolerance=±5% resistance=320 package=THT]
  R19 = Resistor [tolerance=±5% resistance=360 package=THT]
  R20 = Resistor [tolerance=±5% resistance=180 package=THT]
  Monitor = Composite Monitor [package=THT]

nets:
  GND: Pico1.GND, R19.Pin_1, Monitor.pin_3
  N1: Pico1.GP7, R18.Pin_0
  N2: Pico1.GP6, R17.Pin_0
  N3: Pico1.GP5, R15.Pin_0
  N4: Pico1.GP4, R14.Pin_0
  N5: Pico1.GP3, R5.Pin_0
  N6: Pico1.GP2, R4.Pin_0
  N7: Pico1.GP1, R3.Pin_0
  N8: Pico1.GP0, R2.Pin_0
  N9: R2.Pin_1, R7.Pin_0, R19.Pin_0
  N10: R3.Pin_1, R7.Pin_1, R8.Pin_0
  N11: R4.Pin_1, R8.Pin_1, R9.Pin_0
  N12: R5.Pin_1, R9.Pin_1, R10.Pin_0
  N13: R10.Pin_1, R11.Pin_0, R14.Pin_1
  N14: R11.Pin_1, R12.Pin_0, R15.Pin_1
  N15: R12.Pin_1, R17.Pin_1, R20.Pin_0
  N16: R18.Pin_1, R20.Pin_1, Monitor.pin_2

custom parts:
  Raspberry Pi Pico: Raspberry Pi Pico. Based around the RP2040 microcontroller the Pico is a low cost microcontroller device bringing Raspberry Pi quality, cost, and easy of use to the microcontroller space.
  Composite Monitor: Composite Monitor, 75 Ohms
